# Fritzing sketch Untitled Sketch 3 (saved by Fritzing 0.9.4)
breadboards: 1

parts:
  Bauteil1 = Arduino Uno (Rev3)
  hc-sr1 = hc-sr04
  J1 = Basic Servo
  C1 = Capacitor Polarized [package=panasonic_d]

nets:
  N1: Bauteil1.D9_PWM, J1.pulse
  N2: Bauteil1.D10_PWM/SS, hc-sr1.Echo
  N3: Bauteil1.D11_PWM/MOSI, hc-sr1.Trig
  GND: Bauteil1.GND, hc-sr1.GND, J1.gnd, C1.-
  VCC: Bauteil1.5V, hc-sr1.VCC, J1.vcc, C1.+
